// Logisim project F.6.circ as structural Verilog: 8 circuits, main circuit main
module main (
  input  \continue ,
  input  [4:0] test_reg
);

  wire add_en, addi_en, addr_sel_en, Allign, b0_en, b1_en, b2_en, b3_en, clk, is_ram, is_vga, jalr_en,
       load_en, load_misallign, lui_en, not_1_out, not_3_out, not_4_out, or_1_out, or_2_out, PcMisallign,
       por_1_out, por_2_out, ram_write_en, rgb_video_1_p2, rs0_en, rs1_en, stop, store_en, store_misallign,
       vga_write_en, w_en;
  wire [1:0] addr_sel, rs1_sel;
  wire [2:0] rs0_sel, w_sel;
  wire [4:0] add_rd, add_rs0, add_rs1, addi_rd, addi_rs0, jalr_rd, jalr_rs0, load_rd, load_rs0, lui_rd, rs0,
       rs1, store_rs0, store_rs1, w_addr;
  wire [19:0] InsAddr;
  wire [31:0] add_rd_data, adder_1_out, adder_2_out, addi_rdd, gpr_1_test_data, IR, jalr_pc, jalr_rdd,
       load_addr, load_rd_data, lui_rd_data, NextPc, op_addr, PC, ram_read_data, ram_write_data, rdata0,
       rdata1, register_1_q, register_3_q, rom_1_data, store_addr, w_data;

  not not_1 (not_1_out, stop);
  Clock u_clk (.out(clk));
  or or_1 (or_1_out, \continue , not_1_out);
  LED led_1 (.in(or_1_out));
  // Probe on jalr_pc
  // Probe on ram_write_en
  LED led_2 (.in(or_2_out));
  or or_2 (or_2_out, PcMisallign, load_misallign, store_misallign);
  not not_2 (Allign, or_2_out);
  Adder #(.width(32)) adder_1 (.a({PC[31:22], InsAddr, PC[1:0]}), .b(32'h4), .out(adder_1_out));  // open: cin, cout
  Register #(.width(32)) register_1 (.D(jalr_pc), .en(jalr_en), .clk(not_3_out), .Q(register_1_q));  // open: clr
  // Probe on ram_write_data
  Register #(.width(32)) register_2 (.D(adder_1_out), .en(Allign), .clk(clk), .Q(NextPc), .clr(por_1_out));
  POR por_1 (.out(por_1_out));
  or or_3 (PcMisallign, PC[0], PC[1]);
  // Probe on {PC[31:22], InsAddr, PC[1:0]}
  // Probe on op_addr[21:2]
  Multiplexer #(.width(32)) multiplexer_1 (
    .in0(NextPc), .in1(register_1_q), .out({PC[31:22], InsAddr, PC[1:0]}), .sel(jalr_en));
  not not_3 (not_3_out, clk);
  RAM #(.addrWidth(20), .asyncread("true"), .byteenables("byteEnables"), .dataWidth(32), .\type ("nonvolatile")) ram_1 (
    .addr(op_addr[21:2]), .we(ram_write_en), .oe(is_ram), .clk(not_4_out), .din(ram_write_data),
    .dout(ram_read_data), .be3(b3_en), .be2(b2_en), .be1(b1_en), .be0(b0_en));
  not not_4 (not_4_out, clk);
  Adder #(.width(32)) adder_2 (.a(register_3_q), .b(32'h1), .out(adder_2_out));  // open: cin, cout
  // Probe on InsAddr
  // Probe on w_data
  // Probe on w_addr
  // Probe on rs0
  // Probe on rs1
  Register #(.width(32)) register_3 (.D(adder_2_out), .en(1'b1), .clk(clk), .Q(register_3_q));  // open: clr
  ROM #(.addrWidth(20), .dataWidth(32)) rom_1 (.addr(InsAddr), .data(rom_1_data));
  // Probe on ram_read_data
  GPR gpr_1 (
    .clk(not_3_out), .wdata(w_data), .waddr(w_addr), .wen(w_en), .raddr0(rs0), .radd1(rs1),
    .test_addr(test_reg), .rdata0(rdata0), .rdata1(rdata1), .test_data(gpr_1_test_data));
  // Probe on register_3_q
  // Probe on gpr_1_test_data
  Comparator #(.width(32)) comparator_1 (.a(32'h17d4), .b(register_3_q), .eq(stop));  // open: gt, lt
  // Probe on rom_1_data
  // Probe on rdata0
  // Probe on rdata1
  Register #(.width(32)) register_4 (.D(rom_1_data), .en(1'b1), .clk(clk), .Q(IR));  // open: clr
  // Probe on NextPc
  // Probe on rdata0
  POR por_2 (.out(por_2_out));
  // Probe on IR
  // RGB_Video #(.cursor("No Cursor"), .height(256), .width(256)) rgb_video_1: pin names not known; wires that end beside it: por_2_out, rgb_video_1_p2, vga_write_en, op_addr[9:2], op_addr[17:10], ram_write_data[23:0]
  not not_5 (rgb_video_1_p2, clk);
  // Probe on jalr_rs0
  // Probe on addi_rs0
  // Probe on addi_rd
  Multiplexer #(.enable("true"), .select(3), .width(5)) multiplexer_2 (
    .in0(addi_rd), .in1(jalr_rd), .in2(add_rd), .in3(lui_rd), .in4(load_rd), .out(w_addr), .sel(w_sel),
    .en(w_en));  // open: in5, in6, in7
  jalr jalr_1 (
    .OpCode(IR), .APC(NextPc), .Rsd(rdata0), .is_jalr(jalr_en), .rd(jalr_rd), .rs(jalr_rs0), .Rdd(jalr_rdd),
    .NextPc(jalr_pc));
  addi addi_1 (.OpCode(IR), .rsd(rdata0), .is_addi(addi_en), .rd(addi_rd), .rs(addi_rs0), .Rdd(addi_rdd));
  Priority_Encoder priority_encoder_1 (
    .in0(addi_en), .in1(jalr_en), .in2(add_en), .in3(lui_en), .in4(load_en), .out(w_sel), .gs(w_en));  // open: in5, in6, in7, en_in, en_out
  Multiplexer #(.enable("true"), .select(3), .width(32)) multiplexer_3 (
    .in0(addi_rdd), .in1(jalr_rdd), .in2(add_rd_data), .in3(lui_rd_data), .in4(load_rd_data), .out(w_data),
    .sel(w_sel), .en(w_en));  // open: in5, in6, in7
  // Probe on addi_rdd
  Priority_Encoder priority_encoder_2 (
    .in0(addi_en), .in1(jalr_en), .in2(add_en), .in3(load_en), .in4(store_en), .out(rs0_sel), .gs(rs0_en));  // open: in5, in6, in7, en_in, en_out
  Multiplexer #(.enable("true"), .select(3), .width(5)) multiplexer_4 (
    .in0(addi_rs0), .in1(jalr_rs0), .in2(add_rs0), .in3(load_rs0), .in4(store_rs0), .out(rs0), .sel(rs0_sel),
    .en(rs0_en));  // open: in5, in6, in7
  add add_1 (
    .OpCode(IR), .rs0_data(rdata0), .rs1_data(rdata1), .is_add(add_en), .rd(add_rd), .rs0(add_rs0),
    .rs1(add_rs1), .rd_data(add_rd_data));
  lui lui_1 (.OpCode(IR), .is_lui(lui_en), .rd(lui_rd), .rd_data(lui_rd_data));
  // Probe on rs0_sel
  Priority_Encoder #(.select(2)) priority_encoder_3 (
    .in0(add_en), .in1(store_en), .out(rs1_sel), .gs(rs1_en));  // open: in2, in3, en_out, en_in
  Multiplexer #(.enable("true"), .select(2), .width(5)) multiplexer_5 (
    .in0(add_rs1), .in1(store_rs1), .out(rs1), .sel(rs1_sel), .en(rs1_en));  // open: in2, in3
  load load_1 (
    .OpCode(IR), .rs0_data(rdata0), .addr_data(ram_read_data), .is_load(load_en), .rd(load_rd),
    .rs0(load_rs0), .misallign(load_misallign), .addr(load_addr), .rd_data(load_rd_data));
  store store_1 (
    .OpCode(IR), .rs0_data(rdata0), .rs1_data(rdata1), .is_store(store_en), .rs0(store_rs0),
    .misallign(store_misallign), .rs1(store_rs1), .store_addr(store_addr), .store_data(ram_write_data),
    .b_sel({b3_en, b2_en, b1_en, b0_en}));
  Priority_Encoder #(.select(2)) priority_encoder_4 (
    .in0(load_en), .in1(store_en), .out(addr_sel), .gs(addr_sel_en));  // open: in2, in3, en_out, en_in
  // Probe on {op_addr[31:30], is_vga, op_addr[28:0]}
  Multiplexer #(.enable("true"), .select(2), .width(32)) multiplexer_6 (
    .in0(load_addr), .in1(store_addr), .out({op_addr[31:30], is_vga, op_addr[28:0]}), .sel(addr_sel),
    .en(addr_sel_en));  // open: in2, in3
  // Probe on op_addr[21:2]
  and and_1 (ram_write_en, store_en, is_ram);
  not not_6 (is_ram, is_vga);
  and and_2 (vga_write_en, store_en, is_vga);

  // Other names for the same wires on the sheet: b_select[3:0] = {b3_en, b2_en, b1_en, b0_en};
  //   ram_addr[19:0] = op_addr[21:2]; op_addr[29] = is_vga; PC[21:2] = InsAddr; store_data[31:0] = ram_write_data;
  //   vga_write_data[23:0] = ram_write_data[23:0]; vga_x[7:0] = op_addr[9:2]; vga_y[7:0] = op_addr[17:10]

  // Notes on the sheet:
  //   contents of rom_1 (hex, n*v repeats v):
  //   413 93137 10113 10b7 dbc08093 80e7 fe012823 fea10923 fea12423 fe914203 fe4109a3 ff012783 f787b3
  //   f787b3 4b6b7 f0068693 fdc10113 d787b3 10000713 f12423 10593 100793 b00513 2112023 12023 12223 e12623
  //   e12823 f10a23 10b7 a8408093 80e7 2012083 2410113 8067 ff410113 112423 10b7 a7c08093 80e7 513 1800093
  //   80e7 812083 513 c10113 8067 852583 feb12823 fe812e23 3437 a0840413 ff014183 3401b3 1c183 ff114203
  //   440233 24203 4181b3 ff214203 440233 24203 4181b3 ff314203 440233 24203 4181b3 3237 a0020213 320233
  //   24203 ffc12403 420233 420233 410233 11b7 85c18193 fe312823 14800193 fe312623 fec22203 20067 1052703
  //   52683 452783 fe810113 e12423 112a23 fed12823 fef12623 13737 c0070713 fe012223 ff314203 fe4102a3
  //   fef14203 fe410223 fe412203 470233 24203 fe4105a3 ff214203 fe4102a3 fee14203 fe410223 fe412203 470233
  //   24203 fe410523 ff114203 fe4102a3 fed14203 fe410223 fe412203 470233 24203 fe4104a3 ff014203 fe4102a3
  //   fec14203 fe410223 fe412203 470233 24203 fe410423 fe812703 c52603 fee12823 fe812e23 3437 a0840413
  //   ff014183 3401b3 1c183 ff114203 440233 24203 4181b3 ff214203 440233 24203 4181b3 ff314203 440233
  //   24203 4181b3 3237 a0020213 320233 24203 ffc12403 420233 420233 410233 66800193 fe312823 28000193
  //   fe312623 fec22203 20067 c68733 10000513 fe812e23 fe912c23 fee12823 50413 ff012483 fe812423 feb14183
  //   3181b3 fe312423 fe914183 3181b3 fe912423 feb14203 420233 fe412423 fe914203 4181b3 3181b3 fe312a23
  //   fe912423 33237 b0020213 feb14183 4181b3 1c183 fe3103a3 fea14183 4181b3 1c183 fe310323 fe914183
  //   4181b3 1c183 fe3102a3 fe814183 4181b3 1c183 fe310223 ff412183 fe412203 440233 120213 fe412423
  //   feb14203 420233 fe412423 fe914203 4181b3 3237 b0820213 320233 ff812483 ffc12403 24203 420233 420233
  //   410233 11b7 86018193 fe312823 38800193 fe312623 fec22203 20067 812703 10000513 812823 e78733
  //   fe812e23 fe912c23 fee12823 50413 ff012483 fe812423 feb14183 3181b3 fe312423 fe914183 3181b3 fe912423
  //   feb14203 420233 fe412423 fe914203 4181b3 3181b3 fe312a23 fe912423 33237 b0020213 feb14183 4181b3
  //   1c183 fe3103a3 fea14183 4181b3 1c183 fe310323 fe914183 4181b3 1c183 fe3102a3 fe814183 4181b3 1c183
  //   fe310223 ff412183 fe412203 440233 120213 fe412423 feb14203 420233 fe412423 fe914203 4181b3 3237
  //   b0820213 320233 ff812483 ffc12403 24203 420233 420233 410233 11b7 86418193 fe312823 49800193
  //   fe312623 fec22203 20067 8*f787b3 d787b3 f787b3 f787b3 20000437 f40433 812783 c60633 c60633 fef12423
  //   feb14183 3181b3 fe312423 fe914183 fff78213 fe412423 feb14203 420233 fe412423 fe914203 4181b3 3237
  //   b1820213 418233 24203 420233 420233 410233 65800193 fe312823 53c00193 fe312623 fec22203 20067 912623
  //   493 40513 c12223 b12023 10b7 de008093 80e7 12583 412603 812783 148493 40040413 c585b3 fef12823
  //   fe912623 fe812e23 fe912c23 4b437 d0040413 ff014183 340233 100193 320023 fec14183 3401b3 18023 24183
  //   ff114483 940233 100493 920023 fed14483 9404b3 48023 24483 9181b3 ff214483 940233 100493 920023
  //   fee14483 9404b3 48023 24483 9181b3 ff314483 940233 100493 920023 fef14483 9404b3 48023 24483 9181b3
  //   3237 a0020213 320233 24203 ff812483 ffc12403 420233 420233 410233 65400193 fe312823 54400193
  //   fe312623 fec22203 20067 c12483 1012403 1412083 1810113 8067 10000713 fec12823 fee12623 fe812e23
  //   fe912c23 4b437 d0040413 ff014183 340233 100193 320023 fec14183 3401b3 18023 24183 ff114483 940233
  //   100493 920023 fed14483 9404b3 48023 24483 9181b3 ff214483 940233 100493 920023 fee14483 9404b3 48023
  //   24483 9181b3 ff314483 940233 100493 920023 fef14483 9404b3 48023 24483 9181b3 3237 a0020213 320233
  //   24203 ff812483 ffc12403 420233 420233 410233 74c00193 fe312823 28000193 fe312623 fec22203 20067
  //   812703 fee12823 fec12623 fe812e23 fe912c23 4b437 d0040413 ff014183 340233 100193 320023 fec14183
  //   3401b3 18023 24183 ff114483 940233 100493 920023 fed14483 9404b3 48023 24483 9181b3 ff214483 940233
  //   100493 920023 fee14483 9404b3 48023 24483 9181b3 ff314483 940233 100493 920023 fef14483 9404b3 48023
  //   24483 9181b3 3237 a0020213 320233 24203 ff812483 ffc12403 420233 420233 410233 11b7 83418193
  //   fe312823 38800193 fe312623 fec22203 20067 1412083 40637 20000537 1810113 1237 de020213 20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
endmodule

module GPR (
  input  clk,
  input  [31:0] wdata,
  input  [4:0] waddr,
  input  wen,
  input  [4:0] raddr0,
  input  [4:0] radd1,
  input  [4:0] test_addr,
  output [31:0] rdata0,
  output [31:0] rdata1,
  output [31:0] test_data
);

  wire decoder_1_out0, decoder_1_out1, decoder_1_out2, decoder_1_out3, decoder_1_out4, decoder_1_out5,
       decoder_1_out6, decoder_1_out7, decoder_1_out8, decoder_1_out9, decoder_1_out10, decoder_1_out11,
       decoder_1_out12, decoder_1_out13, decoder_1_out14, decoder_1_out15, decoder_1_out16, decoder_1_out17,
       decoder_1_out18, decoder_1_out19, decoder_1_out20, decoder_1_out21, decoder_1_out22, decoder_1_out23,
       decoder_1_out24, decoder_1_out25, decoder_1_out26, decoder_1_out27, decoder_1_out28, decoder_1_out29,
       decoder_1_out30, decoder_1_out31;
  wire [31:0] register_1_q, register_2_q, register_3_q, register_4_q, register_5_q, register_6_q,
       register_7_q, register_8_q, register_9_q, register_10_q, register_11_q, register_12_q, register_13_q,
       register_14_q, register_15_q, register_16_q, register_17_q, register_18_q, register_19_q,
       register_20_q, register_21_q, register_22_q, register_23_q, register_24_q, register_25_q,
       register_26_q, register_27_q, register_28_q, register_29_q, register_30_q, register_31_q,
       register_32_q;

  Decoder #(.select(5)) decoder_1 (
    .out0(decoder_1_out0), .out1(decoder_1_out1), .out2(decoder_1_out2), .out3(decoder_1_out3),
    .out4(decoder_1_out4), .out5(decoder_1_out5), .out6(decoder_1_out6), .out7(decoder_1_out7),
    .out8(decoder_1_out8), .out9(decoder_1_out9), .out10(decoder_1_out10), .out11(decoder_1_out11),
    .out12(decoder_1_out12), .out13(decoder_1_out13), .out14(decoder_1_out14), .out15(decoder_1_out15),
    .out16(decoder_1_out16), .out17(decoder_1_out17), .out18(decoder_1_out18), .out19(decoder_1_out19),
    .out20(decoder_1_out20), .out21(decoder_1_out21), .out22(decoder_1_out22), .out23(decoder_1_out23),
    .out24(decoder_1_out24), .out25(decoder_1_out25), .out26(decoder_1_out26), .out27(decoder_1_out27),
    .out28(decoder_1_out28), .out29(decoder_1_out29), .out30(decoder_1_out30), .out31(decoder_1_out31),
    .sel(waddr), .en(wen));
  Register #(.width(32)) register_1 (.D({32{1'b0}}), .en(decoder_1_out0), .clk(clk), .Q(register_1_q));  // open: clr
  Register #(.width(32)) register_2 (.D(wdata), .en(decoder_1_out8), .clk(clk), .Q(register_2_q));  // open: clr
  Register #(.width(32)) register_3 (.D(wdata), .en(decoder_1_out16), .clk(clk), .Q(register_3_q));  // open: clr
  Register #(.width(32)) register_4 (.D(wdata), .en(decoder_1_out24), .clk(clk), .Q(register_4_q));  // open: clr
  Register #(.width(32)) register_5 (.D(wdata), .en(decoder_1_out1), .clk(clk), .Q(register_5_q));  // open: clr
  Register #(.width(32)) register_6 (.D(wdata), .en(decoder_1_out9), .clk(clk), .Q(register_6_q));  // open: clr
  Register #(.width(32)) register_7 (.D(wdata), .en(decoder_1_out17), .clk(clk), .Q(register_7_q));  // open: clr
  Register #(.width(32)) register_8 (.D(wdata), .en(decoder_1_out25), .clk(clk), .Q(register_8_q));  // open: clr
  Register #(.width(32)) register_9 (.D(wdata), .en(decoder_1_out2), .clk(clk), .Q(register_9_q));  // open: clr
  Register #(.width(32)) register_10 (.D(wdata), .en(decoder_1_out10), .clk(clk), .Q(register_10_q));  // open: clr
  Register #(.width(32)) register_11 (.D(wdata), .en(decoder_1_out18), .clk(clk), .Q(register_11_q));  // open: clr
  Register #(.width(32)) register_12 (.D(wdata), .en(decoder_1_out26), .clk(clk), .Q(register_12_q));  // open: clr
  Register #(.width(32)) register_13 (.D(wdata), .en(decoder_1_out3), .clk(clk), .Q(register_13_q));  // open: clr
  Register #(.width(32)) register_14 (.D(wdata), .en(decoder_1_out11), .clk(clk), .Q(register_14_q));  // open: clr
  Register #(.width(32)) register_15 (.D(wdata), .en(decoder_1_out19), .clk(clk), .Q(register_15_q));  // open: clr
  Register #(.width(32)) register_16 (.D(wdata), .en(decoder_1_out27), .clk(clk), .Q(register_16_q));  // open: clr
  Register #(.width(32)) register_17 (.D(wdata), .en(decoder_1_out4), .clk(clk), .Q(register_17_q));  // open: clr
  Register #(.width(32)) register_18 (.D(wdata), .en(decoder_1_out12), .clk(clk), .Q(register_18_q));  // open: clr
  Register #(.width(32)) register_19 (.D(wdata), .en(decoder_1_out20), .clk(clk), .Q(register_19_q));  // open: clr
  Register #(.width(32)) register_20 (.D(wdata), .en(decoder_1_out28), .clk(clk), .Q(register_20_q));  // open: clr
  Register #(.width(32)) register_21 (.D(wdata), .en(decoder_1_out5), .clk(clk), .Q(register_21_q));  // open: clr
  Register #(.width(32)) register_22 (.D(wdata), .en(decoder_1_out13), .clk(clk), .Q(register_22_q));  // open: clr
  Register #(.width(32)) register_23 (.D(wdata), .en(decoder_1_out21), .clk(clk), .Q(register_23_q));  // open: clr
  Register #(.width(32)) register_24 (.D(wdata), .en(decoder_1_out29), .clk(clk), .Q(register_24_q));  // open: clr
  Register #(.width(32)) register_25 (.D(wdata), .en(decoder_1_out6), .clk(clk), .Q(register_25_q));  // open: clr
  Register #(.width(32)) register_26 (.D(wdata), .en(decoder_1_out14), .clk(clk), .Q(register_26_q));  // open: clr
  Register #(.width(32)) register_27 (.D(wdata), .en(decoder_1_out22), .clk(clk), .Q(register_27_q));  // open: clr
  Register #(.width(32)) register_28 (.D(wdata), .en(decoder_1_out30), .clk(clk), .Q(register_28_q));  // open: clr
  Register #(.width(32)) register_29 (.D(wdata), .en(decoder_1_out7), .clk(clk), .Q(register_29_q));  // open: clr
  Register #(.width(32)) register_30 (.D(wdata), .en(decoder_1_out15), .clk(clk), .Q(register_30_q));  // open: clr
  Register #(.width(32)) register_31 (.D(wdata), .en(decoder_1_out23), .clk(clk), .Q(register_31_q));  // open: clr
  Register #(.width(32)) register_32 (.D(wdata), .en(decoder_1_out31), .clk(clk), .Q(register_32_q));  // open: clr
  Multiplexer #(.select(5), .width(32)) multiplexer_1 (
    .in0(register_1_q), .in1(register_5_q), .in2(register_9_q), .in3(register_13_q), .in4(register_17_q),
    .in5(register_21_q), .in6(register_25_q), .in7(register_29_q), .in8(register_2_q), .in9(register_6_q),
    .in10(register_10_q), .in11(register_14_q), .in12(register_18_q), .in13(register_22_q),
    .in14(register_26_q), .in15(register_30_q), .in16(register_3_q), .in17(register_7_q),
    .in18(register_11_q), .in19(register_15_q), .in20(register_19_q), .in21(register_23_q),
    .in22(register_27_q), .in23(register_31_q), .in24(register_4_q), .in25(register_8_q),
    .in26(register_12_q), .in27(register_16_q), .in28(register_20_q), .in29(register_24_q),
    .in30(register_28_q), .in31(register_32_q), .out(rdata0), .sel(raddr0));
  Multiplexer #(.select(5), .width(32)) multiplexer_2 (
    .in0(register_1_q), .in1(register_5_q), .in2(register_9_q), .in3(register_13_q), .in4(register_17_q),
    .in5(register_21_q), .in6(register_25_q), .in7(register_29_q), .in8(register_2_q), .in9(register_6_q),
    .in10(register_10_q), .in11(register_14_q), .in12(register_18_q), .in13(register_22_q),
    .in14(register_26_q), .in15(register_30_q), .in16(register_3_q), .in17(register_7_q),
    .in18(register_11_q), .in19(register_15_q), .in20(register_19_q), .in21(register_23_q),
    .in22(register_27_q), .in23(register_31_q), .in24(register_4_q), .in25(register_8_q),
    .in26(register_12_q), .in27(register_16_q), .in28(register_20_q), .in29(register_24_q),
    .in30(register_28_q), .in31(register_32_q), .out(rdata1), .sel(radd1));
  Multiplexer #(.select(5), .width(32)) multiplexer_3 (
    .in0(register_1_q), .in1(register_5_q), .in2(register_9_q), .in3(register_13_q), .in4(register_17_q),
    .in5(register_21_q), .in6(register_25_q), .in7(register_29_q), .in8(register_2_q), .in9(register_6_q),
    .in10(register_10_q), .in11(register_14_q), .in12(register_18_q), .in13(register_22_q),
    .in14(register_26_q), .in15(register_30_q), .in16(register_3_q), .in17(register_7_q),
    .in18(register_11_q), .in19(register_15_q), .in20(register_19_q), .in21(register_23_q),
    .in22(register_27_q), .in23(register_31_q), .in24(register_4_q), .in25(register_8_q),
    .in26(register_12_q), .in27(register_16_q), .in28(register_20_q), .in29(register_24_q),
    .in30(register_28_q), .in31(register_32_q), .out(test_data), .sel(test_addr));
endmodule

module addi (
  input  [31:0] OpCode,
  input  [31:0] rsd,
  output is_addi,
  output [4:0] rd,
  output [4:0] rs,
  output [31:0] Rdd
);

  wire comparator_1_eq, comparator_2_eq;
  wire [31:0] imm;

  assign imm = {{20{OpCode[31]}}, OpCode[31:20]};  // Bit_Extender bit_extender_1
  // Probe on imm
  Comparator #(.width(7)) comparator_1 (.a(OpCode[6:0]), .b(7'b0010011), .eq(comparator_1_eq));  // open: gt, lt
  Comparator #(.width(3)) comparator_2 (.a(OpCode[14:12]), .b(3'b000), .eq(comparator_2_eq));  // open: gt, lt
  Adder #(.width(32)) adder_1 (.a(imm), .b(rsd), .out(Rdd));  // open: cin, cout
  and and_1 (is_addi, comparator_1_eq, comparator_2_eq);

  assign rd = OpCode[11:7];
  assign rs = OpCode[19:15];

  // Notes on the sheet:
  //   OpCode: initial=0x1400513
endmodule

module jalr (
  input  [31:0] OpCode,
  input  [31:0] APC,
  input  [31:0] Rsd,
  output is_jalr,
  output [4:0] rd,
  output [4:0] rs,
  output [31:0] Rdd,
  output [31:0] NextPc
);

  wire comparator_1_eq, comparator_2_eq;
  wire [31:0] bit_extender_1_out, imm;

  assign bit_extender_1_out = {{20{OpCode[31]}}, OpCode[31:20]};  // Bit_Extender bit_extender_1
  Adder #(.width(32)) adder_1 (.a(imm), .b(Rsd), .out(NextPc));  // open: cin, cout
  Comparator #(.width(7)) comparator_1 (.a(OpCode[6:0]), .b(7'b1100111), .eq(comparator_1_eq));  // open: gt, lt
  Comparator #(.width(3)) comparator_2 (.a(OpCode[14:12]), .b(3'b000), .eq(comparator_2_eq));  // open: gt, lt
  assign imm = bit_extender_1_out & 32'hfffffffe;  // AND_Gate and_1, 32 bits wide
  and and_2 (is_jalr, comparator_1_eq, comparator_2_eq);

  assign rd = OpCode[11:7];
  assign Rdd = APC;
  assign rs = OpCode[19:15];
endmodule

module add (
  input  [31:0] OpCode,
  input  [31:0] rs0_data,
  input  [31:0] rs1_data,
  output is_add,
  output [4:0] rd,
  output [4:0] rs0,
  output [4:0] rs1,
  output [31:0] rd_data
);

  wire comparator_1_eq, comparator_2_eq;

  Adder #(.width(32)) adder_1 (.a(rs0_data), .b(rs1_data), .out(rd_data));  // open: cin, cout
  Comparator #(.width(7)) comparator_1 (.a(OpCode[6:0]), .b(7'b0110011), .eq(comparator_1_eq));  // open: gt, lt
  Comparator #(.width(3)) comparator_2 (.a(OpCode[14:12]), .b(3'b000), .eq(comparator_2_eq));  // open: gt, lt
  and and_1 (is_add, comparator_1_eq, comparator_2_eq);

  assign rd = OpCode[11:7];
  assign rs0 = OpCode[19:15];
  assign rs1 = OpCode[24:20];

  // Notes on the sheet:
  //   rs0_data: initial=0x1400513
  //   rs1_data: initial=0x1400513
  //   OpCode: initial=0x1400513
endmodule

module lui (
  input  [31:0] OpCode,
  output is_lui,
  output [4:0] rd,
  output [31:0] rd_data
);

  Comparator #(.width(7)) comparator_1 (.a(OpCode[6:0]), .b(7'b0110111), .eq(is_lui));  // open: gt, lt

  assign rd = OpCode[11:7];
  assign rd_data = {OpCode[31:12], {12{1'b0}}};

  // Notes on the sheet:
  //   OpCode: initial=0x1400513
endmodule

module load (
  input  [31:0] OpCode,
  input  [31:0] rs0_data,
  input  [31:0] addr_data,
  output is_load,
  output [4:0] rd,
  output [4:0] rs0,
  output misallign,
  output [31:0] addr,
  output [31:0] rd_data
);

  wire or_1_out;
  wire [0:0] xor_1_out;
  wire [1:0] adder_2_out, and_2_out, index;
  wire [31:0] bit_extender_1_out, bit_extender_2_out, bit_extender_3_out, bit_extender_4_out,
       bit_extender_5_out, bit_extender_6_out, bit_extender_7_out, bit_extender_8_out, bit_extender_9_out,
       bit_extender_10_out, bit_extender_11_out, bit_extender_12_out, bit_extender_13_out,
       bit_extender_14_out, bit_extender_15_out, multiplexer_1_out, multiplexer_2_out, multiplexer_3_out,
       multiplexer_4_out, multiplexer_5_out, multiplexer_6_out, multiplexer_7_out, multiplexer_8_out,
       multiplexer_9_out;
  wire [31:2] adder_1_out;

  assign bit_extender_1_out = {{20{OpCode[31]}}, OpCode[31:20]};  // Bit_Extender bit_extender_1
  Adder #(.width(32)) adder_1 (.a(rs0_data), .b(bit_extender_1_out), .out({adder_1_out, index}));  // open: cin, cout
  Comparator #(.width(7)) comparator_1 (.a(OpCode[6:0]), .b(7'b0000011), .eq(is_load));  // open: gt, lt
  assign addr = {adder_1_out, index} & ~32'h3;  // AND_Gate and_1, 32 bits wide
  assign bit_extender_2_out = {{24{addr_data[7]}}, addr_data[7:0]};  // Bit_Extender bit_extender_2
  assign bit_extender_3_out = {{24{1'b0}}, addr_data[7:0]};  // Bit_Extender bit_extender_3
  assign bit_extender_4_out = {{16{addr_data[15]}}, addr_data[15:0]};  // Bit_Extender bit_extender_4
  assign bit_extender_5_out = {{16{1'b0}}, addr_data[15:0]};  // Bit_Extender bit_extender_5
  assign bit_extender_6_out = {{24{addr_data[15]}}, addr_data[15:8]};  // Bit_Extender bit_extender_6
  assign bit_extender_7_out = {{24{1'b0}}, addr_data[15:8]};  // Bit_Extender bit_extender_7
  assign bit_extender_8_out = {{16{addr_data[23]}}, addr_data[23:8]};  // Bit_Extender bit_extender_8
  assign bit_extender_9_out = {{16{1'b0}}, addr_data[23:8]};  // Bit_Extender bit_extender_9
  assign bit_extender_10_out = {{24{addr_data[23]}}, addr_data[23:16]};  // Bit_Extender bit_extender_10
  assign bit_extender_11_out = {{24{1'b0}}, addr_data[23:16]};  // Bit_Extender bit_extender_11
  assign bit_extender_12_out = {{16{addr_data[31]}}, addr_data[31:16]};  // Bit_Extender bit_extender_12
  assign bit_extender_13_out = {{16{1'b0}}, addr_data[31:16]};  // Bit_Extender bit_extender_13
  assign bit_extender_14_out = {{24{addr_data[31]}}, addr_data[31:24]};  // Bit_Extender bit_extender_14
  assign bit_extender_15_out = {{24{1'b0}}, addr_data[31:24]};  // Bit_Extender bit_extender_15
  Multiplexer #(.width(32)) multiplexer_1 (
    .in0(bit_extender_2_out), .in1(bit_extender_3_out), .out(multiplexer_1_out), .sel(OpCode[14]));
  Multiplexer #(.width(32)) multiplexer_2 (
    .in0(bit_extender_4_out), .in1(bit_extender_5_out), .out(multiplexer_2_out), .sel(OpCode[14]));
  Multiplexer #(.width(32)) multiplexer_3 (
    .in0(bit_extender_6_out), .in1(bit_extender_7_out), .out(multiplexer_3_out), .sel(OpCode[14]));
  Multiplexer #(.width(32)) multiplexer_4 (
    .in0(bit_extender_8_out), .in1(bit_extender_9_out), .out(multiplexer_4_out), .sel(OpCode[14]));
  Multiplexer #(.width(32)) multiplexer_5 (
    .in0(bit_extender_10_out), .in1(bit_extender_11_out), .out(multiplexer_5_out), .sel(OpCode[14]));
  Multiplexer #(.width(32)) multiplexer_6 (
    .in0(bit_extender_12_out), .in1(bit_extender_13_out), .out(multiplexer_6_out), .sel(OpCode[14]));
  Multiplexer #(.width(32)) multiplexer_7 (
    .in0(bit_extender_14_out), .in1(bit_extender_15_out), .out(multiplexer_7_out), .sel(OpCode[14]));
  xor xor_1 (xor_1_out[0], OpCode[13], OpCode[12]);
  Adder #(.width(2)) adder_2 (.a(OpCode[13:12]), .b({1'b0, xor_1_out[0]}), .out(adder_2_out));  // open: cin, cout
  Multiplexer #(.select(2), .width(32)) multiplexer_8 (
    .in0(multiplexer_1_out), .in1(multiplexer_3_out), .in2(multiplexer_5_out), .in3(multiplexer_7_out),
    .out(multiplexer_8_out), .sel(index));
  Multiplexer #(.select(2), .width(32)) multiplexer_9 (
    .in0(multiplexer_2_out), .in1(multiplexer_4_out), .in2(multiplexer_6_out), .out(multiplexer_9_out),
    .sel(index));  // open: in3
  assign and_2_out = adder_2_out & index;  // AND_Gate and_2, 2 bits wide
  or or_1 (or_1_out, and_2_out[0], and_2_out[1]);
  Multiplexer #(.select(2), .width(32)) multiplexer_10 (
    .in0(multiplexer_8_out), .in1(multiplexer_9_out), .in2(addr_data), .in3(addr_data), .out(rd_data),
    .sel(OpCode[13:12]));
  and and_3 (misallign, is_load, or_1_out);

  assign rd = OpCode[11:7];
  assign rs0 = OpCode[19:15];

  // Other names for the same wires on the sheet: width[1:0] = OpCode[13:12]; u = OpCode[14];
  //   imm[11:0] = OpCode[31:20]

  // Notes on the sheet:
  //   rs0_data: initial=0x1400513
  //   addr_data: initial=0x1400513
  //   OpCode: initial=0x1400513
endmodule

module store (
  input  [31:0] OpCode,
  input  [31:0] rs0_data,
  input  [31:0] rs1_data,
  output is_store,
  output [4:0] rs0,
  output misallign,
  output [4:0] rs1,
  output [31:0] store_addr,
  output [31:0] store_data,
  output [3:0] b_sel
);

  wire or_1_out;
  wire [0:0] xor_1_out;
  wire [1:0] adder_2_out, and_2_out, index;
  wire [3:0] multiplexer_4_out, multiplexer_5_out;
  wire [31:0] bit_extender_1_out, multiplexer_1_out, multiplexer_2_out;
  wire [31:2] adder_1_out;

  assign bit_extender_1_out = {{20{OpCode[31]}}, {OpCode[31:25], OpCode[11:7]}};  // Bit_Extender bit_extender_1
  Comparator #(.width(7)) comparator_1 (.a(OpCode[6:0]), .b(7'b0100011), .eq(is_store));  // open: gt, lt
  Adder #(.width(32)) adder_1 (.a(rs0_data), .b(bit_extender_1_out), .out({adder_1_out, index}));  // open: cin, cout
  assign store_addr = {adder_1_out, index} & ~32'h3;  // AND_Gate and_1, 32 bits wide
  Multiplexer #(.select(2), .width(32)) multiplexer_1 (
    .in0({{24{1'b0}}, rs1_data[7:0]}), .in1({{16{1'b0}}, rs1_data[7:0], {8{1'b0}}}),
    .in2({{8{1'b0}}, rs1_data[7:0], {16{1'b0}}}), .in3({rs1_data[7:0], {24{1'b0}}}), .out(multiplexer_1_out),
    .sel(index));
  Multiplexer #(.select(2), .width(32)) multiplexer_2 (
    .in0({{16{1'b0}}, rs1_data[15:0]}), .in1({{8{1'b0}}, rs1_data[15:0], {8{1'b0}}}),
    .in2({rs1_data[15:0], {16{1'b0}}}), .in3({rs1_data[15:0], {16{1'b0}}}), .out(multiplexer_2_out),
    .sel(index));
  Multiplexer #(.select(2), .width(32)) multiplexer_3 (
    .in0(multiplexer_1_out), .in1(multiplexer_2_out), .in2(rs1_data), .in3(rs1_data), .out(store_data),
    .sel(OpCode[13:12]));
  xor xor_1 (xor_1_out[0], OpCode[13], OpCode[12]);
  Adder #(.width(2)) adder_2 (.a(OpCode[13:12]), .b({1'b0, xor_1_out[0]}), .out(adder_2_out));  // open: cin, cout
  assign and_2_out = adder_2_out & index;  // AND_Gate and_2, 2 bits wide
  Multiplexer #(.select(2), .width(4)) multiplexer_4 (
    .in0(4'b0001), .in1(4'b0010), .in2(4'b0100), .in3(4'b1000), .out(multiplexer_4_out), .sel(index));
  Multiplexer #(.select(2), .width(4)) multiplexer_5 (
    .in0(4'b0011), .in1(4'b0110), .in2(4'b1100), .out(multiplexer_5_out), .sel(index));  // open: in3
  or or_1 (or_1_out, and_2_out[0], and_2_out[1]);
  and and_3 (misallign, is_store, or_1_out);
  Multiplexer #(.select(2), .width(4)) multiplexer_6 (
    .in0(multiplexer_4_out), .in1(multiplexer_5_out), .in2(4'b1111), .in3(4'b1111), .out(b_sel),
    .sel(OpCode[13:12]));

  assign rs0 = OpCode[19:15];
  assign rs1 = OpCode[24:20];

  // Other names for the same wires on the sheet: imm[11:0] = {OpCode[31:25], OpCode[11:7]};
  //   width[1:0] = OpCode[13:12]

  // Notes on the sheet:
  //   rs1_data: initial=0x1400513
  //   rs0_data: initial=0x1400513
  //   OpCode: initial=0x1400513
endmodule
