// Logisim project F5.circ as structural Verilog
module sCpu_Rom (
  input  [7:0] Addr0,
  input  [7:0] Addr1,
  input  [7:0] Addr2,
  input  [7:0] Addr3,
  input  [7:0] Addr4,
  input  [7:0] Addr5,
  input  [7:0] Addr6,
  input  [7:0] Addr7,
  input  [3:0] Addr,
  input  [7:0] Addr8,
  input  [7:0] Addr9,
  input  [7:0] Addr10,
  input  [7:0] Addr11,
  input  [7:0] Addr12,
  input  [7:0] Addr13,
  input  [7:0] Addr14,
  input  [7:0] Addr15,
  output [7:0] Q
);

  wire decoder_1_out0, decoder_1_out1, decoder_1_out2, decoder_1_out3, decoder_1_out4, decoder_1_out5,
       decoder_1_out6, decoder_1_out7, decoder_1_out8, decoder_1_out9, decoder_1_out10, decoder_1_out11,
       decoder_1_out12, decoder_1_out13, decoder_1_out14, decoder_1_out15;
  wire [7:0] scpu_8bit_cache_1_q, scpu_8bit_cache_2_q, scpu_8bit_cache_3_q, scpu_8bit_cache_4_q,
       scpu_8bit_cache_5_q, scpu_8bit_cache_6_q, scpu_8bit_cache_7_q, scpu_8bit_cache_8_q,
       scpu_8bit_cache_9_q, scpu_8bit_cache_10_q, scpu_8bit_cache_11_q, scpu_8bit_cache_12_q,
       scpu_8bit_cache_13_q, scpu_8bit_cache_14_q, scpu_8bit_cache_15_q, scpu_8bit_cache_16_q;

  Decoder #(.select(4)) decoder_1 (
    .out0(decoder_1_out0), .out1(decoder_1_out1), .out2(decoder_1_out2), .out3(decoder_1_out3),
    .out4(decoder_1_out4), .out5(decoder_1_out5), .out6(decoder_1_out6), .out7(decoder_1_out7),
    .out8(decoder_1_out8), .out9(decoder_1_out9), .out10(decoder_1_out10), .out11(decoder_1_out11),
    .out12(decoder_1_out12), .out13(decoder_1_out13), .out14(decoder_1_out14), .out15(decoder_1_out15),
    .sel(Addr));  // open: en
  sCpu_8bit_Cache scpu_8bit_cache_1 (.Enable(decoder_1_out0), .Data(Addr0), .Q(scpu_8bit_cache_1_q));
  sCpu_8bit_Cache scpu_8bit_cache_2 (.Enable(decoder_1_out1), .Data(Addr1), .Q(scpu_8bit_cache_2_q));
  sCpu_8bit_Cache scpu_8bit_cache_3 (.Enable(decoder_1_out2), .Data(Addr2), .Q(scpu_8bit_cache_3_q));
  sCpu_8bit_Cache scpu_8bit_cache_4 (.Enable(decoder_1_out3), .Data(Addr3), .Q(scpu_8bit_cache_4_q));
  sCpu_8bit_Cache scpu_8bit_cache_5 (.Enable(decoder_1_out4), .Data(Addr4), .Q(scpu_8bit_cache_5_q));
  sCpu_8bit_Cache scpu_8bit_cache_6 (.Enable(decoder_1_out5), .Data(Addr5), .Q(scpu_8bit_cache_6_q));
  sCpu_8bit_Cache scpu_8bit_cache_7 (.Enable(decoder_1_out6), .Data(Addr6), .Q(scpu_8bit_cache_7_q));
  sCpu_8bit_Cache scpu_8bit_cache_8 (.Enable(decoder_1_out7), .Data(Addr7), .Q(scpu_8bit_cache_8_q));
  sCpu_8bit_Cache scpu_8bit_cache_9 (.Enable(decoder_1_out8), .Data(Addr8), .Q(scpu_8bit_cache_9_q));
  sCpu_8bit_Cache scpu_8bit_cache_10 (.Enable(decoder_1_out9), .Data(Addr9), .Q(scpu_8bit_cache_10_q));
  sCpu_8bit_Cache scpu_8bit_cache_11 (.Enable(decoder_1_out10), .Data(Addr10), .Q(scpu_8bit_cache_11_q));
  sCpu_8bit_Cache scpu_8bit_cache_12 (.Enable(decoder_1_out11), .Data(Addr11), .Q(scpu_8bit_cache_12_q));
  sCpu_8bit_Cache scpu_8bit_cache_13 (.Enable(decoder_1_out12), .Data(Addr12), .Q(scpu_8bit_cache_13_q));
  sCpu_8bit_Cache scpu_8bit_cache_14 (.Enable(decoder_1_out13), .Data(Addr13), .Q(scpu_8bit_cache_14_q));
  sCpu_8bit_Cache scpu_8bit_cache_15 (.Enable(decoder_1_out14), .Data(Addr14), .Q(scpu_8bit_cache_15_q));
  sCpu_8bit_Cache scpu_8bit_cache_16 (.Enable(decoder_1_out15), .Data(Addr15), .Q(scpu_8bit_cache_16_q));
  assign Q = scpu_8bit_cache_1_q | scpu_8bit_cache_2_q | scpu_8bit_cache_3_q | scpu_8bit_cache_4_q | scpu_8bit_cache_5_q | scpu_8bit_cache_6_q | scpu_8bit_cache_7_q | scpu_8bit_cache_8_q | scpu_8bit_cache_9_q | scpu_8bit_cache_10_q | scpu_8bit_cache_11_q | scpu_8bit_cache_12_q | scpu_8bit_cache_13_q | scpu_8bit_cache_14_q | scpu_8bit_cache_15_q | scpu_8bit_cache_16_q;  // OR_Gate or_1, 8 bits wide
endmodule

module sCpu_8bit_Cache (
  input  Enable,
  input  [7:0] Data,
  output [7:0] Q
);

  and and_1 (Q[0], Enable, Data[0]);
  and and_2 (Q[1], Enable, Data[1]);
  and and_3 (Q[2], Enable, Data[2]);
  and and_4 (Q[3], Enable, Data[3]);
  and and_5 (Q[4], Enable, Data[4]);
  and and_6 (Q[5], Enable, Data[5]);
  and and_7 (Q[6], Enable, Data[6]);
  and and_8 (Q[7], Enable, Data[7]);
endmodule

module sCpu_8bit_RwCache (
  input  [7:0] Data,
  input  addr_en,
  input  Clk,
  input  EN,
  output [7:0] Q,
  output [7:0] Qraw
);

  wire and_1_out, and_2_out;

  and and_1 (and_1_out, Clk, EN);
  and and_2 (and_2_out, addr_en, and_1_out);
  and and_3 (Q[7], addr_en, Qraw[7]);
  D_Flip_Flop d_ff_1 (.D(Data[7]), .clk(and_2_out), .Q(Qraw[7]));  // open: Qn, preset, reset
  and and_4 (Q[6], addr_en, Qraw[6]);
  D_Flip_Flop d_ff_2 (.D(Data[6]), .clk(and_2_out), .Q(Qraw[6]));  // open: Qn, preset, reset
  D_Flip_Flop d_ff_3 (.D(Data[5]), .clk(and_2_out), .Q(Qraw[5]));  // open: Qn, preset, reset
  and and_5 (Q[5], addr_en, Qraw[5]);
  D_Flip_Flop d_ff_4 (.D(Data[4]), .clk(and_2_out), .Q(Qraw[4]));  // open: Qn, preset, reset
  and and_6 (Q[4], addr_en, Qraw[4]);
  D_Flip_Flop d_ff_5 (.D(Data[3]), .clk(and_2_out), .Q(Qraw[3]));  // open: Qn, preset, reset
  and and_7 (Q[3], addr_en, Qraw[3]);
  D_Flip_Flop d_ff_6 (.D(Data[2]), .clk(and_2_out), .Q(Qraw[2]));  // open: Qn, preset, reset
  and and_8 (Q[2], addr_en, Qraw[2]);
  D_Flip_Flop d_ff_7 (.D(Data[1]), .clk(and_2_out), .Q(Qraw[1]));  // open: Qn, preset, reset
  and and_9 (Q[1], addr_en, Qraw[1]);
  D_Flip_Flop d_ff_8 (.D(Data[0]), .clk(and_2_out), .Q(Qraw[0]));  // open: Qn, preset, reset
  and and_10 (Q[0], addr_en, Qraw[0]);
endmodule

module sCpu_gpr (
  input  [7:0] Data,
  input  Clk,
  input  En,
  input  [1:0] rIndex,
  output [7:0] R0,
  output [7:0] R1,
  output [7:0] Q,
  output [7:0] R2,
  output [7:0] R3
);

  wire decoder_1_out0, decoder_1_out1, decoder_1_out2, decoder_1_out3;
  wire [7:0] scpu_8bit_rwcache_1_q, scpu_8bit_rwcache_2_q, scpu_8bit_rwcache_3_q, scpu_8bit_rwcache_4_q;

  Decoder #(.select(2)) decoder_1 (
    .out0(decoder_1_out0), .out1(decoder_1_out1), .out2(decoder_1_out2), .out3(decoder_1_out3), .sel(rIndex));  // open: en
  sCpu_8bit_RwCache scpu_8bit_rwcache_1 (
    .Data(Data), .addr_en(decoder_1_out0), .Clk(Clk), .EN(En), .Q(scpu_8bit_rwcache_1_q), .Qraw(R0));
  sCpu_8bit_RwCache scpu_8bit_rwcache_2 (
    .Data(Data), .addr_en(decoder_1_out1), .Clk(Clk), .EN(En), .Q(scpu_8bit_rwcache_2_q), .Qraw(R1));
  sCpu_8bit_RwCache scpu_8bit_rwcache_3 (
    .Data(Data), .addr_en(decoder_1_out2), .Clk(Clk), .EN(En), .Q(scpu_8bit_rwcache_3_q), .Qraw(R2));
  sCpu_8bit_RwCache scpu_8bit_rwcache_4 (
    .Data(Data), .addr_en(decoder_1_out3), .Clk(Clk), .EN(En), .Q(scpu_8bit_rwcache_4_q), .Qraw(R3));
  assign Q = scpu_8bit_rwcache_1_q | scpu_8bit_rwcache_2_q | scpu_8bit_rwcache_3_q | scpu_8bit_rwcache_4_q;  // OR_Gate or_1, 8 bits wide
endmodule

module scpu_li (
);

  wire clock_1_out, comparator_1_eq;
  wire [3:0] scpu_pc_1_pc;
  wire [7:0] bit_extender_1_out, Rom_q, scpu_gpr_1_q, scpu_gpr_1_r0, scpu_gpr_1_r1, scpu_gpr_1_r2,
       scpu_gpr_1_r3;

  Clock clock_1 (.out(clock_1_out));
  scpu_pc scpu_pc_1 (.Clk(clock_1_out), .PC(scpu_pc_1_pc));
  // Probe on scpu_pc_1_pc
  sCpu_Rom Rom (
    .Addr0(8'h81), .Addr1(8'h92), .Addr2(8'ha3), .Addr3(8'hb4), .Addr4({8{1'b0}}), .Addr5(8'h10),
    .Addr6(8'h20), .Addr7(8'h30), .Addr(scpu_pc_1_pc), .Q(Rom_q));  // open: Addr8, Addr9, Addr10, Addr11, Addr12, Addr13, Addr14, Addr15
  sCpu_gpr scpu_gpr_1 (
    .Data(bit_extender_1_out), .Clk(clock_1_out), .En(comparator_1_eq), .rIndex(Rom_q[5:4]),
    .R0(scpu_gpr_1_r0), .R1(scpu_gpr_1_r1), .Q(scpu_gpr_1_q), .R2(scpu_gpr_1_r2), .R3(scpu_gpr_1_r3));
  Comparator #(.width(2)) comparator_1 (.a(Rom_q[7:6]), .b(2'b10), .eq(comparator_1_eq));  // open: gt, lt
  // Probe on Rom_q[5:4]
  assign bit_extender_1_out = {{4{1'b0}}, Rom_q[3:0]};  // Bit_Extender bit_extender_1
  // Probe on scpu_gpr_1_r0
  // Probe on scpu_gpr_1_r1
  // Probe on scpu_gpr_1_q
  // Probe on scpu_gpr_1_r2
  // Probe on scpu_gpr_1_r3
endmodule

module scpu_pc (
  input  Clk,
  output [3:0] PC
);

  wire [3:0] adder_1_out;

  Adder #(.width(4)) adder_1 (.a(PC), .b(4'b0001), .out(adder_1_out));  // open: cin, cout
  Register #(.width(4)) register_1 (.D(adder_1_out), .en(1'b1), .clk(Clk), .Q(PC));  // open: clr
endmodule

module sCpu_8bitRwCache_ext (
  input  [7:0] WData,
  input  raddr0,
  input  waddr,
  input  Clk,
  input  WEn,
  input  raddr1,
  output [7:0] rdata0,
  output [7:0] rdata1,
  output [7:0] rraw
);

  wire and_1_out, and_2_out;

  and and_1 (and_1_out, Clk, WEn);
  and and_2 (and_2_out, waddr, and_1_out);
  and and_3 (rdata0[7], raddr0, rraw[7]);
  D_Flip_Flop d_ff_1 (.D(WData[7]), .clk(and_2_out), .Q(rraw[7]));  // open: Qn, preset, reset
  and and_4 (rdata1[7], raddr1, rraw[7]);
  and and_5 (rdata0[6], raddr0, rraw[6]);
  D_Flip_Flop d_ff_2 (.D(WData[6]), .clk(and_2_out), .Q(rraw[6]));  // open: Qn, preset, reset
  D_Flip_Flop d_ff_3 (.D(WData[5]), .clk(and_2_out), .Q(rraw[5]));  // open: Qn, preset, reset
  and and_6 (rdata1[6], raddr1, rraw[6]);
  and and_7 (rdata0[5], raddr0, rraw[5]);
  D_Flip_Flop d_ff_4 (.D(WData[4]), .clk(and_2_out), .Q(rraw[4]));  // open: Qn, preset, reset
  and and_8 (rdata1[5], raddr1, rraw[5]);
  and and_9 (rdata0[4], raddr0, rraw[4]);
  D_Flip_Flop d_ff_5 (.D(WData[3]), .clk(and_2_out), .Q(rraw[3]));  // open: Qn, preset, reset
  and and_10 (rdata1[4], raddr1, rraw[4]);
  and and_11 (rdata0[3], raddr0, rraw[3]);
  D_Flip_Flop d_ff_6 (.D(WData[2]), .clk(and_2_out), .Q(rraw[2]));  // open: Qn, preset, reset
  and and_12 (rdata1[3], raddr1, rraw[3]);
  and and_13 (rdata0[2], raddr0, rraw[2]);
  D_Flip_Flop d_ff_7 (.D(WData[1]), .clk(and_2_out), .Q(rraw[1]));  // open: Qn, preset, reset
  and and_14 (rdata1[2], raddr1, rraw[2]);
  and and_15 (rdata0[1], raddr0, rraw[1]);
  and and_16 (rdata1[1], raddr1, rraw[1]);
  D_Flip_Flop d_ff_8 (.D(WData[0]), .clk(and_2_out), .Q(rraw[0]));  // open: Qn, preset, reset
  and and_17 (rdata0[0], raddr0, rraw[0]);
  and and_18 (rdata1[0], raddr1, rraw[0]);
endmodule

module scpu_gpr_ext (
  input  [7:0] WData,
  input  Clk,
  input  WEn,
  input  [1:0] raddr0,
  input  [1:0] raddr1,
  input  [1:0] waddr,
  output [7:0] rdata0,
  output [7:0] rdata1,
  output [7:0] r0,
  output [7:0] r1,
  output [7:0] r2,
  output [7:0] r3
);

  wire decoder_1_out0, decoder_1_out1, decoder_1_out2, decoder_1_out3, decoder_2_out0, decoder_2_out1,
       decoder_2_out2, decoder_2_out3, decoder_3_out0, decoder_3_out1, decoder_3_out2, decoder_3_out3;
  wire [7:0] scpu_8bitrwcache_ext_1_rdata0, scpu_8bitrwcache_ext_1_rdata1, scpu_8bitrwcache_ext_2_rdata0,
       scpu_8bitrwcache_ext_2_rdata1, scpu_8bitrwcache_ext_3_rdata0, scpu_8bitrwcache_ext_3_rdata1,
       scpu_8bitrwcache_ext_4_rdata0, scpu_8bitrwcache_ext_4_rdata1;

  Decoder #(.select(2)) decoder_1 (
    .out0(decoder_1_out0), .out1(decoder_1_out1), .out2(decoder_1_out2), .out3(decoder_1_out3), .sel(waddr));  // open: en
  Decoder #(.select(2)) decoder_2 (
    .out0(decoder_2_out0), .out1(decoder_2_out1), .out2(decoder_2_out2), .out3(decoder_2_out3), .sel(raddr0));  // open: en
  Decoder #(.select(2)) decoder_3 (
    .out0(decoder_3_out0), .out1(decoder_3_out1), .out2(decoder_3_out2), .out3(decoder_3_out3), .sel(raddr1));  // open: en
  sCpu_8bitRwCache_ext scpu_8bitrwcache_ext_1 (
    .WData(WData), .raddr0(decoder_2_out0), .waddr(decoder_1_out0), .Clk(Clk), .WEn(WEn),
    .raddr1(decoder_3_out0), .rdata0(scpu_8bitrwcache_ext_1_rdata0), .rdata1(scpu_8bitrwcache_ext_1_rdata1),
    .rraw(r0));
  sCpu_8bitRwCache_ext scpu_8bitrwcache_ext_2 (
    .WData(WData), .raddr0(decoder_2_out1), .waddr(decoder_1_out1), .Clk(Clk), .WEn(WEn),
    .raddr1(decoder_3_out1), .rdata0(scpu_8bitrwcache_ext_2_rdata0), .rdata1(scpu_8bitrwcache_ext_2_rdata1),
    .rraw(r1));
  sCpu_8bitRwCache_ext scpu_8bitrwcache_ext_3 (
    .WData(WData), .raddr0(decoder_2_out2), .waddr(decoder_1_out2), .Clk(Clk), .WEn(WEn),
    .raddr1(decoder_3_out2), .rdata0(scpu_8bitrwcache_ext_3_rdata0), .rdata1(scpu_8bitrwcache_ext_3_rdata1),
    .rraw(r2));
  sCpu_8bitRwCache_ext scpu_8bitrwcache_ext_4 (
    .WData(WData), .raddr0(decoder_2_out3), .waddr(decoder_1_out3), .Clk(Clk), .WEn(WEn),
    .raddr1(decoder_3_out3), .rdata0(scpu_8bitrwcache_ext_4_rdata0), .rdata1(scpu_8bitrwcache_ext_4_rdata1),
    .rraw(r3));
  assign rdata0 = scpu_8bitrwcache_ext_1_rdata0 | scpu_8bitrwcache_ext_2_rdata0 | scpu_8bitrwcache_ext_3_rdata0 | scpu_8bitrwcache_ext_4_rdata0;  // OR_Gate or_1, 8 bits wide
  assign rdata1 = scpu_8bitrwcache_ext_1_rdata1 | scpu_8bitrwcache_ext_2_rdata1 | scpu_8bitrwcache_ext_3_rdata1 | scpu_8bitrwcache_ext_4_rdata1;  // OR_Gate or_2, 8 bits wide
endmodule

module scpu_add (
  input  [7:0] ins,
  input  [7:0] rrs1,
  input  [7:0] rrs2,
  output [1:0] rs2,
  output [1:0] rs1,
  output [1:0] rd,
  output [7:0] rrd
);

  Adder adder_1 (.a(rrs1), .b(rrs2), .out(rrd));  // open: cin, cout

  assign rd = ins[5:4];
  assign rs1 = ins[3:2];
  assign rs2 = ins[1:0];
endmodule

module scpu (
);

  wire Add, bner0, bner0_jmp, clock_1_out, hex_display_1_a, hex_display_1_b, hex_display_1_c,
       hex_display_1_d, hex_display_1_e, hex_display_1_f, hex_display_1_g, hex_display_1_h, hex_display_2_a,
       hex_display_2_b, hex_display_2_c, hex_display_2_d, hex_display_2_e, hex_display_2_f, hex_display_2_g,
       hex_display_2_h, jen, li, not_1_out, out_rs, priority_encoder_1_gs, WEn;
  wire [1:0] add_rd, add_rs1, add_rs2, bner0_rs1, bner0_rs2, li_rd, out_rs1, priority_encoder_1_out, rd, rs1,
       rs2;
  wire [3:0] jaddr, PC_pc, register_1_q, scpu_out_1_datah, scpu_out_1_datal;
  wire [7:0] add_rrd, imm, ins, Regs_r0, Regs_r1, Regs_r2, Regs_r3, Regs_rdata0, Regs_rdata1, wdata;

  Clock clock_1 (.out(clock_1_out));
  and and_1 (jen, bner0, bner0_jmp);
  or or_1 (WEn, Add, li);
  scpu_pc_ext PC (.Clk(clock_1_out), .jaddr(jaddr), .jmp(jen), .PC(PC_pc));
  Multiplexer #(.width(8)) multiplexer_1 (.in0(imm), .in1(add_rrd), .out(wdata), .sel(Add));
  Multiplexer #(.width(2)) multiplexer_2 (.in0(li_rd), .in1(add_rd), .out(rd), .sel(Add));
  Register #(.width(4)) register_1 (.D(PC_pc), .en(1'b1), .clk(clock_1_out), .Q(register_1_q));  // open: clr
  not not_1 (not_1_out, clock_1_out);
  Priority_Encoder #(.select(2)) priority_encoder_1 (
    .in0(Add), .in1(bner0), .in2(out_rs), .out(priority_encoder_1_out), .gs(priority_encoder_1_gs));  // open: in3, en_out, en_in
  sCpu_Rom Rom (
    .Addr0(8'h8b), .Addr1(8'h91), .Addr2(8'ha0), .Addr3(8'hb2), .Addr4(8'h29), .Addr5(8'h17), .Addr6(8'hd1),
    .Addr7(8'h48), .Addr(register_1_q), .Addr8(8'hdf), .Q(ins));  // open: Addr9, Addr10, Addr11, Addr12, Addr13, Addr14, Addr15
  Multiplexer #(.width(2)) multiplexer_3 (.in0(bner0_rs2), .in1(add_rs2), .out(rs2), .sel(Add));
  // Probe on rs1
  Multiplexer #(.enable("true"), .select(2), .width(2)) multiplexer_4 (
    .in0(add_rs1), .in1(bner0_rs1), .in2(out_rs1), .out(rs1), .sel(priority_encoder_1_out),
    .en(priority_encoder_1_gs));  // open: in3
  // Probe on rs2
  // Probe on wdata
  // Probe on rd
  Decoder #(.select(2)) decoder_1 (.out0(Add), .out1(out_rs), .out2(li), .out3(bner0), .sel(ins[7:6]));  // open: en
  // Probe on ins
  scpu_gpr_ext Regs (
    .WData(wdata), .Clk(not_1_out), .WEn(WEn), .raddr0(rs1), .raddr1(rs2), .waddr(rd), .rdata0(Regs_rdata0),
    .rdata1(Regs_rdata1), .r0(Regs_r0), .r1(Regs_r1), .r2(Regs_r2), .r3(Regs_r3));
  // Probe on Regs_rdata0
  // Probe on Regs_rdata1
  // Probe on PC_pc
  // Probe on Regs_r0
  // Probe on Regs_r1
  // Probe on Regs_r2
  // Probe on Regs_r3
  scpu_li_v2 scpu_li_v2_1 (.ins(ins), .imm(imm), .rd(li_rd));
  scpu_add scpu_add_1 (
    .ins(ins), .rrs1(Regs_rdata0), .rrs2(Regs_rdata1), .rs2(add_rs2), .rs1(add_rs1), .rd(add_rd),
    .rrd(add_rrd));
  // Probe on imm
  // Probe on li_rd
  // Probe on add_rs1
  scpu_bner0 scpu_bner0_1 (
    .ins(ins), .rrs2(Regs_rdata1), .rrs1(Regs_rdata0), .rs2(bner0_rs2), .addr(jaddr), .rs1(bner0_rs1),
    .jmp(bner0_jmp));
  scpu_out scpu_out_1 (
    .ins(ins), .rrs1(Regs_rdata0), .rs1(out_rs1), .datal(scpu_out_1_datal), .datah(scpu_out_1_datah));
  // Probe on add_rs2
  // Probe on bner0_rs2
  // Probe on bner0_rs1
  hex_display hex_display_1 (
    .En(out_rs), .data(scpu_out_1_datal), .h(hex_display_1_h), .a(hex_display_1_a), .b(hex_display_1_b),
    .c(hex_display_1_c), .d(hex_display_1_d), .e(hex_display_1_e), .f(hex_display_1_f), .g(hex_display_1_g));
  hex_display hex_display_2 (
    .En(out_rs), .data(scpu_out_1_datah), .h(hex_display_2_h), .a(hex_display_2_a), .b(hex_display_2_b),
    .c(hex_display_2_c), .d(hex_display_2_d), .e(hex_display_2_e), .f(hex_display_2_f), .g(hex_display_2_g));
  _7_Segment_Display u_7_segment_display_1 (
    .g(hex_display_2_g), .f(hex_display_2_f), .a(hex_display_2_a), .b(hex_display_2_b), .e(hex_display_2_e),
    .d(hex_display_2_d), .c(hex_display_2_c), .dp(hex_display_2_h));
  _7_Segment_Display u_7_segment_display_2 (
    .g(hex_display_1_g), .f(hex_display_1_f), .a(hex_display_1_a), .b(hex_display_1_b), .e(hex_display_1_e),
    .d(hex_display_1_d), .c(hex_display_1_c), .dp(hex_display_1_h));
endmodule

module scpu_pc_ext (
  input  Clk,
  input  [3:0] jaddr,
  input  jmp,
  output [3:0] PC
);

  wire [3:0] adder_1_out, register_1_q;

  Adder #(.width(4)) adder_1 (.a(PC), .b(4'b0001), .out(adder_1_out));  // open: cin, cout
  Register #(.width(4)) register_1 (.D(adder_1_out), .en(1'b1), .clk(Clk), .Q(register_1_q));  // open: clr
  Multiplexer #(.width(4)) multiplexer_1 (.in0(register_1_q), .in1(jaddr), .out(PC), .sel(jmp));
endmodule

module scpu_li_v2 (
  input  [7:0] ins,
  output [7:0] imm,
  output [1:0] rd
);

  assign imm = {{4{1'b0}}, ins[3:0]};  // Bit_Extender bit_extender_1

  assign rd = ins[5:4];
endmodule

module scpu_bner0 (
  input  [7:0] ins,
  input  [7:0] rrs2,
  input  [7:0] rrs1,
  output [1:0] rs2,
  output [3:0] addr,
  output [1:0] rs1,
  output jmp
);

  wire comparator_1_eq;

  Comparator comparator_1 (.a(rrs2), .b(rrs1), .eq(comparator_1_eq));  // open: gt, lt
  not not_1 (jmp, comparator_1_eq);

  assign addr = ins[5:2];
  assign rs1 = 2'b00;
  assign rs2 = ins[1:0];
endmodule

module scpu_out (
  input  [7:0] ins,
  input  [7:0] rrs1,
  output [1:0] rs1,
  output [3:0] datal,
  output [3:0] datah
);


  assign datah = rrs1[7:4];
  assign datal = rrs1[3:0];
  assign rs1 = ins[3:2];
endmodule

module hex_display (
  input  En,
  input  [3:0] data,
  output h,
  output a,
  output b,
  output c,
  output d,
  output e,
  output f,
  output g
);

  wire ap, bp, cp, dp, ep, fp, gp, hp, n0, n1, n2, n3, n4, n5, n6, n7, n8, n9, n10, n11, n12, n13, n14, n15,
       or_1_out, or_2_out, or_3_out, or_4_out, or_5_out, or_6_out, or_7_out;

  or or_1 (or_1_out, gp, n15, n10, n13, n11, n14, n14);
  or or_2 (or_2_out, ap, ap, n10, n12, n12, n14, n15);
  or or_3 (or_3_out, bp, bp, n13, n13, n13, n10, n10);
  or or_4 (or_4_out, cp, cp, n10, n11, n11, n13, n13);
  or or_5 (or_5_out, dp, dp, n12, n11, n11, n13, n14);
  or or_6 (or_6_out, ep, n15, n12, n10, n11, n13, n14);
  or or_7 (or_7_out, fp, n15, n12, n10, n11, n14, n14);
  Decoder #(.select(4)) decoder_1 (
    .out0(n0), .out1(n1), .out2(n2), .out3(n3), .out4(n4), .out5(n5), .out6(n6), .out7(n7), .out8(n8),
    .out9(n9), .out10(n10), .out11(n11), .out12(n12), .out13(n13), .out14(n14), .out15(n15), .sel(data),
    .en(En));
  and and_1 (h, ~1'b1, hp);  // AND_Gate
  and and_2 (a, ~h, or_2_out);  // AND_Gate
  and and_3 (b, ~h, or_3_out);  // AND_Gate
  and and_4 (c, ~h, or_4_out);  // AND_Gate
  and and_5 (d, ~h, or_5_out);  // AND_Gate
  and and_6 (e, ~h, or_6_out);  // AND_Gate
  and and_7 (f, ~h, or_7_out);  // AND_Gate
  and and_8 (g, ~h, or_1_out);  // AND_Gate
  or or_8 (ap, n0, n2, n3, n5, n6, n7, n8, n9, n9);
  or or_9 (bp, n0, n1, n2, n3, n4, n7, n8, n9, n9);
  or or_10 (cp, n0, n1, n3, n4, n5, n6, n7, n8, n9);
  or or_11 (dp, n0, n2, n3, n5, n5, n6, n8, n8, n9);
  or or_12 (ep, n0, n2, n6, n8, n8, n8, n8, n8, n8);
  or or_13 (fp, n0, n4, n5, n6, n8, n9, n9, n9, n9);
  or or_14 (gp, n2, n2, n3, n4, n5, n6, n6, n8, n9);
  nor nor_1 (hp, n2, n0, n1, n3, n4, n6, n7, n8, n9, n5);
endmodule
